// Digital circuit main.dig as structural Verilog
module main (
  input  clk,
  input  in_2,
  input  [1:0] in_5,
  output IP_plus__plus,
  output [1:0] TO
);

  wire comparator_1_eq, fetch, RESET;
  wire [1:0] micro_step;
  wire [1:1] iseq;
  wire [3:0] micro_addr;
  wire [7:0] data, RAM_D, RF_s;
  wire [9:0] ADDR;
  wire [15:0] AX, BX, CX, DX, Rg_tmp;

  ROM #(.AddrBits(10), .Bits(8)) PRG (.A(ADDR), .sel(in_2), .D(data));
  Button button_1 (.out(RESET));
  sequenser #(.applicationType("IVERILOG")) u_sequenser (
    .RESET(RESET), .clk(clk), .aseq(micro_addr), .iseq({TO, iseq[1], IP_plus__plus}), .fetch(fetch),
    .count(micro_step));
  CPU #(.applicationType("IVERILOG")) u_CPU (
    .RESET(RESET), .clk(clk), .iseq({TO, iseq[1], IP_plus__plus}), .fetch(fetch), .DATAB(data), .IP(ADDR),
    .OP(micro_addr), .AX(AX), .CX(CX), .DX(DX), .BX(BX), .RgTMP(Rg_tmp), .RFsrc(RF_s));
  Comparator #(.Bits(2)) comparator_1 (.a(TO), .b(in_5), .eq(comparator_1_eq));  // open: gt, lt
  BlockRAMDualPort #(.AddrBits(16), .Bits(8)) blockramdualport_1 (
    .A(Rg_tmp), .Din(RF_s), .str(comparator_1_eq), .C(clk), .D(RAM_D));

  // Other names for the same wires on the sheet: iseq (some bits) = {TO, IP_plus__plus}; wr = iseq[1]

  // Notes on the sheet:
  //   in_2: default 1
  //   in_5: default 2
  //   contents of PRG (hex, n*v repeats v):
  //   b0,aa,a0,30
endmodule

/* Code of sequenser:
`define FETCH_BIT 4

module sequenser(
  input  RESET,
  input  clk,
  input  [3:0]aseq, 
  output [`FETCH_BIT-1:0]iseq,
  output reg fetch = 1'b1,
  output reg [1:0]count = 2'd0
);

reg [`FETCH_BIT:0]sequence[63:0];

always@(posedge clk or posedge RESET) begin
  if(RESET) begin
     fetch <= 1'b1;
     count <= 2'd0;
/* start                             F TO W IP    * /
     sequence[{2'b00, 4'b0000}] = 5'b0_00_0_0;
// 1011.0.reg  op=1011 d=0 --> op.d.reg #const8 (B0 AA)  MOV AL, 0xAA
     sequence[{2'b00, 4'b1011}] = 5'b0_00_0_1;
     sequence[{2'b01, 4'b1011}] = 5'b1_00_1_1;
     sequence[{2'b10, 4'b1011}] = 5'b0_00_0_0;
     sequence[{2'b11, 4'b1011}] = 5'b0_00_0_0;
// 1010.000.w addr_l addr_h w=0 -> A0 00 30  MOV AL, byte ptr [0x3000]
     sequence[{2'b00, 4'b1010}] = 5'b0_00_0_1;
     sequence[{2'b01, 4'b1010}] = 5'b0_01_1_1;
     sequence[{2'b10, 4'b1010}] = 5'b0_01_1_1;
     sequence[{2'b11, 4'b1010}] = 5'b1_10_1_1;
  end else begin
     fetch <= sequence[{count, aseq}][`FETCH_BIT];
     count <= (fetch)? 2'd0 : (count + 1'b1);
  end
end

assign iseq = sequence[{count, aseq}][(`FETCH_BIT-1):0];
endmodule
*/

/* Code of CPU:
module CPU(
  input  RESET,
  input  clk,
  input  [3:0]iseq,
  input  fetch,
  input  [7:0]DATAB,
  output reg [9:0]IP,
  output [3:0]OP,
  output [15:0]AX,
  output [15:0]CX,
  output [15:0]DX,
  output [15:0]BX,
  output reg [15:0]RgTMP,
  output [7:0]RFsrc
);

reg [7:0]RF[7:0];
reg [7:0]OP_CODE;

wire REG_WR, INC_IP;
wire [1:0]target;
wire [2:0]rg;
wire d;

assign {OP,d,rg} = OP_CODE;
assign {target, REG_WR, INC_IP} = iseq;

wire toRF = (target == 2'b00);
wire toTMP = (target == 2'b01);

always@(posedge clk or posedge RESET) begin
  if(RESET) begin
     IP <= 10'd0;
     OP_CODE <= 8'd0;
  end else begin
     if(fetch) OP_CODE <= DATAB[7:0];
     IP <= IP + INC_IP;
     if(toRF & REG_WR) RF[rg] <= DATAB[7:0];
     if(toTMP) begin
        RgTMP[7:0] <= RgTMP[15:8];
        RgTMP[15:8] <= DATAB;
     end;
  end
end
assign AX = {RF[4], RF[0]};
assign CX = {RF[5], RF[1]};
assign DX = {RF[6], RF[2]};
assign BX = {RF[7], RF[3]};
assign RFsrc = RF[rg];
endmodule
*/
